// Logisim project booth_algo.circ as structural Verilog: 2 circuits, main circuit main
module main (
  input  [15:0] M,
  input  Signal_In,
  output [31:0] Product,
  output [15:0] Q,
  output [15:0] A
);

  wire clock_1_out;
  wire [15:0] multiplier_16bits_1_ac_write, multiplier_16bits_1_mq_write;

  Clock clock_1 (.out(clock_1_out));
  Multiplier_16bits multiplier_16bits_1 (
    .X(M), .MQ_Read(Product[15:0]), .AC_Read(A), .Signal_In(Signal_In), .CLK(clock_1_out),
    .MQ_Write(multiplier_16bits_1_mq_write), .AC_Write(multiplier_16bits_1_ac_write));  // open: Signal_Out
  Register #(.width(16)) AC (.D(multiplier_16bits_1_ac_write), .en(1'b1), .clk(clock_1_out), .Q(A), .clr(1'b0));
  Register #(.width(16)) MQ (
    .D(multiplier_16bits_1_mq_write), .en(1'b1), .clk(clock_1_out), .Q(Product[15:0]), .clr(1'b0));

  assign Product[31:16] = A;
  assign Q = Product[15:0];
endmodule

module Multiplier_16bits (
  input  [15:0] X,
  input  [15:0] MQ_Read,
  input  [15:0] AC_Read,
  input  Signal_In,
  input  CLK,
  output [15:0] MQ_Write,
  output [15:0] AC_Write,
  output Signal_Out
);

  wire and_1_out, and_2_out, and_3_out, and_4_out, and_5_out, and_6_out, and_7_out, counter_1_carry,
       d_ff_2_q, d_ff_3_q, not_1_out, or_1_out, or_2_out, or_3_out;
  wire [0:0] d_ff_1_q;
  wire [15:0] adder_1_out, multiplexer_1_out, multiplexer_2_out, multiplexer_3_out, multiplexer_4_out,
       multiplexer_5_out, subtractor_1_out;
  wire [32:0] shifter_1_out;

  or or_1 (or_1_out, and_1_out, and_2_out);
  and and_1 (and_1_out, ~Signal_In, shifter_1_out[0], or_2_out);  // AND_Gate
  and and_2 (and_2_out, ~Signal_In, ~or_2_out, d_ff_1_q[0]);  // AND_Gate
  D_Flip_Flop d_ff_1 (.D(or_1_out), .clk(CLK), .Q(d_ff_1_q[0]), .reset(1'b0));  // open: Qn, preset
  Subtractor #(.width(16)) subtractor_1 (.a(AC_Read), .b(X), .out(subtractor_1_out), .bin(1'b0));  // open: bout
  Adder #(.width(16)) adder_1 (.a(AC_Read), .b(X), .out(adder_1_out), .cin(1'b0));  // open: cout
  Shifter #(.shift("ar"), .width(33)) shifter_1 (
    .in({AC_Read, MQ_Read, d_ff_1_q[0]}), .\dist (6'b000001), .out(shifter_1_out));
  or or_2 (or_2_out, and_3_out, and_4_out, not_1_out);
  and and_3 (and_3_out, ~d_ff_1_q[0], ~MQ_Read[0]);  // AND_Gate
  and and_4 (and_4_out, d_ff_1_q[0], MQ_Read[0]);
  not not_1 (not_1_out, d_ff_2_q);
  D_Flip_Flop d_ff_2 (.D(or_2_out), .clk(CLK), .Q(d_ff_2_q), .reset(1'b0));  // open: Qn, preset
  Multiplexer #(.width(16)) multiplexer_1 (
    .in0(subtractor_1_out), .in1(adder_1_out), .out(multiplexer_1_out), .sel(and_5_out));
  and and_5 (and_5_out, d_ff_1_q[0], ~MQ_Read[0]);  // AND_Gate
  Multiplexer #(.width(16)) multiplexer_2 (
    .in0(MQ_Read), .in1(shifter_1_out[16:1]), .out(multiplexer_2_out), .sel(or_2_out));
  Multiplexer #(.width(16)) multiplexer_3 (
    .in0(multiplexer_1_out), .in1(shifter_1_out[32:17]), .out(multiplexer_3_out), .sel(or_2_out));
  Multiplexer #(.width(16)) multiplexer_4 (
    .in0(multiplexer_2_out), .in1(MQ_Read), .out(multiplexer_4_out), .sel(Signal_In));
  Multiplexer #(.width(16)) multiplexer_5 (
    .in0(multiplexer_3_out), .in1({16{1'b0}}), .out(multiplexer_5_out), .sel(Signal_In));
  Counter #(.max('h3f), .ongoal("stay"), .width(6)) counter_1 (
    .clr(1'b0), .load(Signal_In), .up(1'b0), .count(or_2_out), .clk(CLK), .D(6'b010000),
    .carry(counter_1_carry));  // open: Q
  Multiplexer #(.width(16)) multiplexer_6 (.in0(AC_Read), .in1(multiplexer_5_out), .out(AC_Write), .sel(or_3_out));
  or or_3 (or_3_out, and_6_out, and_7_out);
  Multiplexer #(.width(16)) multiplexer_7 (.in0(MQ_Read), .in1(multiplexer_4_out), .out(MQ_Write), .sel(or_3_out));
  and and_6 (and_6_out, Signal_In, counter_1_carry);
  and and_7 (and_7_out, d_ff_3_q, ~counter_1_carry);  // AND_Gate
  D_Flip_Flop d_ff_3 (.D(or_3_out), .clk(CLK), .Q(d_ff_3_q), .reset(1'b0));  // open: Qn, preset
  and and_8 (Signal_Out, ~or_3_out, d_ff_3_q);  // AND_Gate
endmodule
